# Fritzing sketch devre (saved by Fritzing 0.9.3b)
circuit board: 6.02737cm x 6.24405cm

parts:
  Kutahya = female pin header, 13 pins [form="♀ (female)"]
  Il_Ozel_Idaresi = female pin header, 13 pins [form="♀ (female)"]
  RFID = female pin header, 8 pins [form="♀ (female)"]
  OLED = female pin header, 4 pins [form="♀ (female)"]
  Buzzer = female pin header, 4 pins [form="♀ (female)"]
  K_LED = female pin header, 2 pins [form="♀ (female)"]
  Y_LED = female pin header, 2 pins [form="♀ (female)"]
  ROLE = female pin header, 3 pins [form="♀ (female)"]
  Parça1 = Arduino Nano (Rev3.0) (ICSP)
  R1 = Resistor [tolerance=±5% resistance=100k package=THT]

nets:
  N1: Kutahya.pin1, RFID.pin1
  N2: Kutahya.pin2, OLED.pin4
  N3: Kutahya.pin3, OLED.pin3
  N4: Kutahya.pin4, Parça1.D7, R1.Pin_0
  N5: Kutahya.pin5, Kutahya.pin13, Il_Ozel_Idaresi.pin4, Il_Ozel_Idaresi.pin7, Il_Ozel_Idaresi.pin11, RFID.pin3, OLED.pin1, Buzzer.pin1, ROLE.pin3, Parça1.GND, R1.Pin_1
  N6: Kutahya.pin10, RFID.pin6
  N7: Kutahya.pin11, RFID.pin5
  N8: Kutahya.pin12, RFID.pin7
  N9: Il_Ozel_Idaresi.pin2, RFID.pin8
  N10: Il_Ozel_Idaresi.pin3, RFID.pin2
  N11: Il_Ozel_Idaresi.pin5, K_LED.pin2, Y_LED.pin2
  N12: Il_Ozel_Idaresi.pin6, K_LED.pin1, Y_LED.pin1
  N13: Il_Ozel_Idaresi.pin12, Il_Ozel_Idaresi.pin13, OLED.pin2, ROLE.pin2, Parça1.VIN
  N14: Buzzer.pin4, Parça1.D8
  N15: ROLE.pin1, Parça1.D9
